// Digital circuit display-module.dig as structural Verilog
module display_module (
  input  [7:0] D,
  input  [1:0] S
);

  wire [7:0] demultiplexer_1_out_0, demultiplexer_1_out_1, demultiplexer_1_out_2, demultiplexer_1_out_3;

  Seven_Seg #(.persistTime(8)) seven_seg_1 (
    .a(demultiplexer_1_out_3[0]), .b(demultiplexer_1_out_3[1]), .c(demultiplexer_1_out_3[2]),
    .d(demultiplexer_1_out_3[3]), .e(demultiplexer_1_out_3[4]), .f(demultiplexer_1_out_3[5]),
    .g(demultiplexer_1_out_3[6]), .dp(demultiplexer_1_out_3[7]));
  Demultiplexer #(.Selector_Bits(2), .Bits(8)) demultiplexer_1 (
    .sel(S), .in(D), .out_0(demultiplexer_1_out_0), .out_1(demultiplexer_1_out_1),
    .out_2(demultiplexer_1_out_2), .out_3(demultiplexer_1_out_3));
  Seven_Seg #(.persistTime(8)) seven_seg_2 (
    .a(demultiplexer_1_out_2[0]), .b(demultiplexer_1_out_2[1]), .c(demultiplexer_1_out_2[2]),
    .d(demultiplexer_1_out_2[3]), .e(demultiplexer_1_out_2[4]), .f(demultiplexer_1_out_2[5]),
    .g(demultiplexer_1_out_2[6]), .dp(demultiplexer_1_out_2[7]));
  Seven_Seg #(.persistTime(8)) seven_seg_3 (
    .a(demultiplexer_1_out_1[0]), .b(demultiplexer_1_out_1[1]), .c(demultiplexer_1_out_1[2]),
    .d(demultiplexer_1_out_1[3]), .e(demultiplexer_1_out_1[4]), .f(demultiplexer_1_out_1[5]),
    .g(demultiplexer_1_out_1[6]), .dp(demultiplexer_1_out_1[7]));
  Seven_Seg #(.persistTime(8)) seven_seg_4 (
    .a(demultiplexer_1_out_0[0]), .b(demultiplexer_1_out_0[1]), .c(demultiplexer_1_out_0[2]),
    .d(demultiplexer_1_out_0[3]), .e(demultiplexer_1_out_0[4]), .f(demultiplexer_1_out_0[5]),
    .g(demultiplexer_1_out_0[6]), .dp(demultiplexer_1_out_0[7]));
endmodule
