// Digital circuit 2c.dig as structural Verilog
module _2c (
  input  [7:0] A,
  input  Cin,
  output [7:0] X,
  output Cout
);

  wire add8b_1_cout, not_2_out;
  wire [7:0] not_1_out;

  assign not_1_out = ~A;  // Not not_1, 8 bits wide
  not not_2 (not_2_out, Cin);
  add8b add8b_1 (.A(not_1_out), .B(8'h1), .Cin(1'b0), .X(X), .Cout(add8b_1_cout));
  add1b add1b_1 (.A(not_2_out), .B(1'b0), .Cin(add8b_1_cout), .X(Cout));  // open: Cout
endmodule
