// Digital circuit add4b.dig as structural Verilog
module add4b (
  input  A0,
  input  A1,
  input  A2,
  input  A3,
  input  B0,
  input  B1,
  input  B2,
  input  B3,
  input  Cin,
  output Cout,
  output X0,
  output X1,
  output X2,
  output X3
);

  wire add1b_1_cout, add1b_2_cout, add1b_3_cout;

  add1b add1b_1 (.A(A0), .B(B0), .Cin(Cin), .X(X0), .Cout(add1b_1_cout));
  add1b add1b_2 (.A(A1), .B(B1), .Cin(add1b_1_cout), .X(X1), .Cout(add1b_2_cout));
  add1b add1b_3 (.A(A2), .B(B2), .Cin(add1b_2_cout), .X(X2), .Cout(add1b_3_cout));
  add1b add1b_4 (.A(A3), .B(B3), .Cin(add1b_3_cout), .X(X3), .Cout(Cout));
endmodule
