// Digital circuit add8b.dig as structural Verilog
module add8b (
  input  [7:0] A,
  input  [7:0] B,
  input  Cin,
  output [7:0] X,
  output Cout
);

  wire add1b_1_cout, add1b_2_cout, add1b_3_cout, add1b_4_cout, add1b_5_cout, add1b_6_cout, add1b_7_cout;

  add1b add1b_1 (.A(A[0]), .B(B[0]), .Cin(Cin), .X(X[0]), .Cout(add1b_1_cout));
  add1b add1b_2 (.A(A[1]), .B(B[1]), .Cin(add1b_1_cout), .X(X[1]), .Cout(add1b_2_cout));
  add1b add1b_3 (.A(A[2]), .B(B[2]), .Cin(add1b_2_cout), .X(X[2]), .Cout(add1b_3_cout));
  add1b add1b_4 (.A(A[3]), .B(B[3]), .Cin(add1b_3_cout), .X(X[3]), .Cout(add1b_4_cout));
  add1b add1b_5 (.A(A[4]), .B(B[4]), .Cin(add1b_4_cout), .X(X[4]), .Cout(add1b_5_cout));
  add1b add1b_6 (.A(A[5]), .B(B[5]), .Cin(add1b_5_cout), .X(X[5]), .Cout(add1b_6_cout));
  add1b add1b_7 (.A(A[6]), .B(B[6]), .Cin(add1b_6_cout), .X(X[6]), .Cout(add1b_7_cout));
  add1b add1b_8 (.A(A[7]), .B(B[7]), .Cin(add1b_7_cout), .X(X[7]), .Cout(Cout));
endmodule
