// Digital circuit add8bs.dig as structural Verilog
module add8bs (
  input  [7:0] A,
  input  [7:0] B,
  input  Cin,
  output [7:0] X,
  output Cout
);

  wire add8b_1_cout;

  add8b add8b_1 (.A(A), .B(B), .Cin(Cin), .X(X), .Cout(add8b_1_cout));
  add1b add1b_1 (.A(A[7]), .B(B[7]), .Cin(add8b_1_cout), .X(Cout));  // open: Cout
endmodule
