// Digital circuit bcd-decoder.dig as structural Verilog
module bcd_decoder (
  input  [3:0] I,
  output [7:0] X
);

  LookUpTable #(.Bits(8)) lookuptable_1 (.in0(I[0]), .in1(I[1]), .in2(I[2]), .in3(I[3]), .out(X));

  // Notes on the sheet:
  //   X: 7-segment display signals
  //   I: BCD decimal
  //   contents of lookuptable_1 (hex, n*v repeats v):
  //   3f,6,5b,4f,66,6d,7d,7,7f,6f
endmodule
