// Digital circuit bcd2disp.dig as structural Verilog
module bcd2disp (
  input  [3:0] N0,
  input  [3:0] N1,
  input  [3:0] N2,
  input  [3:0] N3,
  input  CLK
);

  wire [1:0] display_driver_1_s;
  wire [7:0] bcd_decoder_1_x, bcd_decoder_2_x, bcd_decoder_3_x, bcd_decoder_4_x, demultiplexer_1_out_0,
       demultiplexer_1_out_1, demultiplexer_1_out_2, demultiplexer_1_out_3, display_driver_1_d;

  bcd_decoder bcd_decoder_1 (.I(N0), .X(bcd_decoder_1_x));
  bcd_decoder bcd_decoder_2 (.I(N1), .X(bcd_decoder_2_x));
  bcd_decoder bcd_decoder_3 (.I(N2), .X(bcd_decoder_3_x));
  bcd_decoder bcd_decoder_4 (.I(N3), .X(bcd_decoder_4_x));
  display_driver display_driver_1 (
    .CLK(CLK), .D0(bcd_decoder_1_x), .D1(bcd_decoder_2_x), .D2(bcd_decoder_3_x), .D3(bcd_decoder_4_x),
    .D(display_driver_1_d), .S(display_driver_1_s));
  display_module display_module_1 (.D(display_driver_1_d), .S(display_driver_1_s));
  Seven_Seg #(.persistTime(8)) seven_seg_1 (
    .a(demultiplexer_1_out_3[0]), .b(demultiplexer_1_out_3[1]), .c(demultiplexer_1_out_3[2]),
    .d(demultiplexer_1_out_3[3]), .e(demultiplexer_1_out_3[4]), .f(demultiplexer_1_out_3[5]),
    .g(demultiplexer_1_out_3[6]), .dp(demultiplexer_1_out_3[7]));
  Demultiplexer #(.Selector_Bits(2), .Bits(8)) demultiplexer_1 (
    .sel(display_driver_1_s), .in(display_driver_1_d), .out_0(demultiplexer_1_out_0),
    .out_1(demultiplexer_1_out_1), .out_2(demultiplexer_1_out_2), .out_3(demultiplexer_1_out_3));
  Seven_Seg #(.persistTime(8)) seven_seg_2 (
    .a(demultiplexer_1_out_2[0]), .b(demultiplexer_1_out_2[1]), .c(demultiplexer_1_out_2[2]),
    .d(demultiplexer_1_out_2[3]), .e(demultiplexer_1_out_2[4]), .f(demultiplexer_1_out_2[5]),
    .g(demultiplexer_1_out_2[6]), .dp(demultiplexer_1_out_2[7]));
  Seven_Seg #(.persistTime(8)) seven_seg_3 (
    .a(demultiplexer_1_out_1[0]), .b(demultiplexer_1_out_1[1]), .c(demultiplexer_1_out_1[2]),
    .d(demultiplexer_1_out_1[3]), .e(demultiplexer_1_out_1[4]), .f(demultiplexer_1_out_1[5]),
    .g(demultiplexer_1_out_1[6]), .dp(demultiplexer_1_out_1[7]));
  Seven_Seg #(.persistTime(8)) seven_seg_4 (
    .a(demultiplexer_1_out_0[0]), .b(demultiplexer_1_out_0[1]), .c(demultiplexer_1_out_0[2]),
    .d(demultiplexer_1_out_0[3]), .e(demultiplexer_1_out_0[4]), .f(demultiplexer_1_out_0[5]),
    .g(demultiplexer_1_out_0[6]), .dp(demultiplexer_1_out_0[7]));
endmodule
