// Digital circuit bin2bcd.dig as structural Verilog
module bin2bcd (
  input  [7:0] A,
  output [3:0] X,
  output [7:0] R
);

  wire [7:4] div_1_r;

  Div #(.Bits(8)) div_1 (.a(A), .b(8'ha), .q(R), .r({div_1_r, X}));
endmodule
