// Digital circuit display-driver.dig as structural Verilog
module display_driver (
  input  CLK,
  input  [7:0] D0,
  input  [7:0] D1,
  input  [7:0] D2,
  input  [7:0] D3,
  output [7:0] D,
  output [1:0] S
);

  Multiplexer #(.Selector_Bits(2), .Bits(8)) multiplexer_1 (
    .sel(S), .in_0(D0), .in_1(D1), .in_2(D2), .in_3(D3), .out(D));
  Counter #(.Bits(2)) counter_1 (.en(1'b1), .C(CLK), .clr(1'b0), .out(S));  // open: ovf
endmodule
