// Digital circuit min8b.dig as structural Verilog
module min8b (
  input  [7:0] A,
  input  [7:0] B,
  input  Cin,
  output [7:0] X,
  output Cout
);

  wire _2c_1_cout, add8b_1_cout;
  wire [7:0] _2c_1_x;

  _2c _2c_1 (.A(B), .Cin(B[7]), .X(_2c_1_x), .Cout(_2c_1_cout));
  add8b add8b_1 (.A(A), .B(_2c_1_x), .Cin(Cin), .X(X), .Cout(add8b_1_cout));
  add1b add1b_1 (.A(A[7]), .B(_2c_1_cout), .Cin(add8b_1_cout), .X(Cout));  // open: Cout
endmodule
