// Digital circuit rr8b.dig as structural Verilog
module rr8b (
  input  [7:0] A,
  input  [7:0] S,
  output [7:0] X
);

  wire [7:0] min8b_1_x;

  min8b min8b_1 (.A(8'h8), .B(S), .Cin(1'b0), .X(min8b_1_x));  // open: Cout
  rl8b rl8b_1 (.A(A), .S(min8b_1_x), .X(X));

  // Notes on the sheet:
  //   S: Shift amount
endmodule
