// Digital circuit sr8b.dig as structural Verilog
module sr8b (
  input  [7:0] A,
  input  [7:0] S,
  output [7:0] X
);

  BarrelShifter #(.Bits(8), .direction("right")) barrelshifter_1 (.in(A), .shift(S[3:0]), .out(X));

  // Notes on the sheet:
  //   S: Shift amount
endmodule
