// Digital circuit stopp.dig as structural Verilog
module stopp (
  input  [7:0] A,
  output [7:0] X
);

  wire [7:0] _2c_1_x;

  _2c _2c_1 (.A(A), .X(_2c_1_x));
  Multiplexer #(.Bits(8)) multiplexer_1 (.sel(A[7]), .in_0(A), .in_1(_2c_1_x), .out(X));
endmodule
