// Digital circuit add1b.dig as structural Verilog
module add1b (
  input  A,
  input  B,
  input  Cin,
  output X,
  output Cout
);

  wire half_add_1_cout, half_add_1_x, half_add_2_cout;

  half_add half_add_1 (.A(A), .B(B), .X(half_add_1_x), .Cout(half_add_1_cout));
  half_add half_add_2 (.A(Cin), .B(half_add_1_x), .X(X), .Cout(half_add_2_cout));
  or or_1 (Cout, half_add_2_cout, half_add_1_cout);
endmodule
